# Fritzing sketch 433Hz_Rx_Tx_LED_Button (saved by Fritzing 0.9.3b)
breadboards: 2

parts:
  Mod1 = KY-002 Vibration Switch Module [package="Breakout board"]
  U1 = RF-LINK_TX [package=rf-link_tx]
  YwRobot_Power_Supply1 = YwRobot Breadboard Power Supply [part_number=545043]
  Composant1 = Arduino Mega 2560 (Rev3)
  Composant5 = Arduino Uno (Rev3)
  U5 = RF-LINK_RX [package=rf-link_rx]
  LED3 = smd LED [color="Red (633nm)" package="1206 [SMD]"]
  R3 = Resistor [tolerance=±5% resistance=220 package="0805 [SMD]"]

nets:
  N1: Mod1.S, Composant1.D6_PWM
  VIN: Mod1.Vin, U1.+5V, YwRobot_Power_Supply1.VCC_-_Power_Supply_Double_5v-3v
  N2: Mod1.-, U1.ANT, YwRobot_Power_Supply1.GND#11, Composant1.GND
  N3: U1.DATA, Composant1.D12_PWM
  N4: Composant5.D6_PWM, R3.Pin_1
  N5: Composant5.GND, U5.ANT, LED3.cathode
  N6: LED3.anode, R3.Pin_0

notes:
  433Hz RX Module has 4 PINS at th eRight
  4 PIN at the Left doesn't existe
  433Hz TX Module has 3 PINS
  1 PIN at the Left doesn't existe

custom parts:
  KY-002 Vibration Switch Module: Arduino Vibration Switch Module KY-002 Keyes allows detection of shock and vibration.
  YwRobot Breadboard Power Supply: The YwRobot Breadboard Power Supply (MB-V2) has two power rails; they can be 5V or 3V3. Power to the module can be provided through the female USB socket or through the A10 (female) 2.1mm power jack.

// code stored in the sketch: 433Hz_Rx_LED_Button.ino
#include <VirtualWire.h>
#define ledPin 6

void setup()
{
  Serial.begin(9600);
  vw_set_rx_pin(11);
  vw_setup(2000);
  pinMode(ledPin, OUTPUT);
  vw_rx_start();
}

void loop()
{
    uint8_t buf[VW_MAX_MESSAGE_LEN];
    uint8_t buflen = VW_MAX_MESSAGE_LEN; 
    Serial.print("Data = ");
    Serial.println(VW_MAX_MESSAGE_LEN);
    if (vw_get_message(buf, &buflen))
    {
      if(buf[0]=='a')
      {  
       digitalWrite(ledPin,HIGH);
      }  
      else if(buf[0]=='b')
      {
       digitalWrite(ledPin,LOW);
      }
    }
    delay(500);
}

// code stored in the sketch: 433Hz_Tx_LED_Button.ino
#include <VirtualWire.h>

#define button 6


char *data;
int val;
int value = 0;

void setup() 
{
  Serial.begin(9600);
  pinMode(button, INPUT);
  vw_set_tx_pin(12);
  vw_setup(2000);
  pinMode(button, INPUT_PULLUP);
}

void loop()
{
  val = digitalRead(button);
  if(val == LOW && value == 0)
  {
    const char *data="a";
    Serial.print("data sent = ");
    Serial.println(data);
    Serial.println("LED ON");
    vw_send((uint8_t *)data, strlen(data));
    vw_wait_tx();
    delay(300);
    value = 1;
  }
  else if(val == LOW && value == 1)
  {
    const char *data="b";
    Serial.print("data sent = ");
    Serial.println(data);
    Serial.println("LED OFF");
    vw_send((uint8_t *)data, strlen(data));
    vw_wait_tx();
    delay(300);
    value = 0;
  }
  //delay(200);
}
